# Fritzing sketch Car_LCD_Display (saved by Fritzing 0.7.10b)
perfboards: 2

parts:
  J1 = screw terminal, 3 pins
  R1 = Resistor [tolerance=±5% resistance=100k package=THT]
  R2 = Resistor [tolerance=±5% resistance=100k package=THT]
  R3 = Resistor [tolerance=±1% resistance=47k package=THT]
  R4 = Resistor [tolerance=±1% resistance=47k package=THT]
  J2 = female pin header, 4 pins [form="♀ (female)"]
  Arduino1 = Arduino
  8x1_LCD = LCD screen
  LCD_backlight_dimmer = Rotary Potentiometer (Large) [maximum_resistance=25kΩ package=THT]
  S1 = Pushbutton [package="[THT]"]
  S2 = Pushbutton [package="[THT]"]
  T1 = DS18B20 Temperature Sensor [part_number=DS18B20 package="TO92 [THT]"]
  R5 = Resistor [tolerance=±5% resistance=10k package=THT]
  R6 = Resistor [tolerance=±5% resistance=10k package=THT]
  R7 = Resistor [tolerance=±5% resistance=4.7k package=THT]
  T2 = DS18B20 Temperature Sensor [part_number=DS18B20 package="TO92 [THT]"]
  D1 = Rectifier Diode [part_number=1N4007 package="300 mil [THT]"]

nets:
  GND: J1.pin1, R3.Pin_0, R4.Pin_0, J2.pin1, Arduino1.GND, 8x1_LCD.VSS, 8x1_LCD.R/W, LCD_backlight_dimmer.wiper, S1.Pin_3, S1.Pin_4, S2.Pin_3, S2.Pin_4, T1.GND, T2.GND, D1.cathode
  N1: J1.pin2, R1.Pin_1, J2.pin2, Arduino1.VIN
  N2: J1.pin3, R2.Pin_1
  N3: R1.Pin_0, R3.Pin_1, J2.pin3, Arduino1.A1
  N4: R2.Pin_0, R4.Pin_1, J2.pin4, Arduino1.D7
  N5: Arduino1.D12, 8x1_LCD.RS
  N6: Arduino1.D11, 8x1_LCD.E
  N7: Arduino1.D10, S1.Pin_1, S1.Pin_2, R5.Pin_0
  N8: Arduino1.D9, S2.Pin_1, S2.Pin_2, R6.Pin_0
  N9: Arduino1.D8, T1.DQ, R7.Pin_0, T2.DQ
  N10: Arduino1.D6, 8x1_LCD.LED+
  N11: Arduino1.D5, 8x1_LCD.DB4
  N12: Arduino1.D4, 8x1_LCD.DB5
  N13: Arduino1.D3, 8x1_LCD.DB6
  N14: Arduino1.D2, 8x1_LCD.DB7
  +5V: Arduino1.+5V, 8x1_LCD.VDD, T1.+Vdd, R5.Pin_1, R6.Pin_1, R7.Pin_1, T2.+Vdd
  N15: 8x1_LCD.V0, D1.anode
  N16: 8x1_LCD.LED-, LCD_backlight_dimmer.leg2

notes:
  Arduino car LCD display
  For more info visit:
  KristoZ.com

custom parts:
  DS18B20 Temperature Sensor: A DS18B20 temperature sensor
