# Fritzing sketch power_supply_board (saved by Fritzing 0.7.10b)
perfboards: 1

parts:
  J1 = screw terminal, 3 pins
  J2 = female pin header, 4 pins [form="♀ (female)"]
  R5 = Resistor [tolerance=±5% resistance=100k package=THT]
  R6 = Resistor [tolerance=±5% resistance=100k package=THT]
  R3 = Resistor [tolerance=±1% resistance=47k package=THT]
  R4 = Resistor [tolerance=±1% resistance=47k package=THT]

nets:
  N1: J1.pin1, J2.pin1, R3.Pin_0, R4.Pin_0
  N2: J1.pin2, J2.pin2, R6.Pin_1
  N3: J1.pin3, R5.Pin_1
  N4: J2.pin3, R6.Pin_0, R3.Pin_1
  N5: J2.pin4, R5.Pin_0, R4.Pin_1
